# Fritzing sketch full_bridge (saved by Fritzing 0.9.4)
breadboards: 1

parts:
  part = LOAD_CELL [package=1x03]
  part_2 = LOAD_CELL [package=1x03]
  part_3 = LOAD_CELL [package=1x03]
  part_4 = LOAD_CELL [package=1x03]
  part_5 = HX711 Weighing Sensor Module
  Part1 = Photon

nets:
  N1: part.B, part_2.B, part_5.E+
  N2: part.R, part_3.R, part_5.A-
  N3: part_2.R, part_4.R, part_5.A+
  N4: part_3.B, part_4.B, part_5.E-
  VCC: part_5.VCC, Part1.VIN
  GND: part_5.GND, Part1.GND
  N5: part_5.DO/RX, Part1.D3
  N6: part_5.CK/TX, Part1.D2
